# Fritzing sketch Pedometer_PCB (saved by Fritzing 0.9.3b)
circuit board: 6.00184cm x 3.29461cm
breadboards: 1

parts:
  Battery = LIPO-110mAh [package=lipo-110]  # not connected
  J4 = female pin header, 4 pins [form="♀ (female)"]
  OLED_I2C1 = OLED 128x64 I2C Monochrome Display  # not connected
  Pins_of_Tp-4056 = female pin header, 1 pin [form="♀ (female)"]
  part = female pin header, 1 pin [form="♀ (female)"]
  Pro_Mini = Arduino Pro Mini v13
  part_2 = female pin header, 4 pins [form="♀ (female)"]
  Part1 = Bluetooth HM-10  # not connected

nets (from the breadboard view):
  N1: J4.pin1, Pro_Mini.VCC, part_2.pin4
  N2: J4.pin2, Pins_of_Tp-4056.pin1, Pro_Mini.GND, part_2.pin3
  N3: J4.pin3, Pro_Mini.A5, part_2.pin2
  N4: J4.pin4, Pro_Mini.A4, part_2.pin1
  N5: part.pin1, Pro_Mini.RAW

notes:
  Kevin Witaszek
  Tp-4056
  KX023 Pins
  KX023 Sensor
  I2C
  TXD/RXD
  KX023
  OLED
  +
  -
  HM-10
