# Fritzing sketch SmartWatch_PCB (saved by Fritzing 0.9.3b)
circuit board: 5.07528cm x 3.33023cm
breadboards: 1

parts:
  Button = Pushbutton [package=THT]
  Battery = LIPO-110mAh [package=lipo-110]
  Pro_Mini = Arduino Pro Mini v13
  HM-10_Pins = female pin header, 4 pins [form="♀ (female)"]
  Pins_of_Tp-4056 = female pin header, 2 pins [form="♀ (female)"]
  Pins_of_Tp-4056_2 = female pin header, 2 pins [form="♀ (female)"]
  J4 = female pin header, 4 pins [form="♀ (female)"]
  OLED_screen_Pins = female pin header, 4 pins [form="♀ (female)"]
  TP1 = TP4056 [chip_label=TP4056 package="DIP (Dual Inline) [THT]"]
  Part1 = Bluetooth HM-10  # not connected
  OLED_I2C1 = OLED 128x64 I2C Monochrome Display  # not connected

nets:
  N1: Button.leg0, Pro_Mini.D2
  N2: Button.leg1, Pro_Mini.GND, HM-10_Pins.pin3, Pins_of_Tp-4056_2.pin2, J4.pin2, OLED_screen_Pins.pin3
  N3: Battery.+, TP1.pin4
  N4: Battery.-, TP1.pin5
  N5: Pro_Mini.VCC, HM-10_Pins.pin4, J4.pin1, OLED_screen_Pins.pin4
  N6: Pro_Mini.A4, J4.pin4, OLED_screen_Pins.pin1
  N7: Pro_Mini.A5, J4.pin3, OLED_screen_Pins.pin2
  N8: Pro_Mini.RAW, Pins_of_Tp-4056.pin1
  N9: Pro_Mini.D10_PWM/SS, HM-10_Pins.pin1
  N10: Pro_Mini.D9_PWM, HM-10_Pins.pin2
  N11: Pins_of_Tp-4056.pin2, TP1.pin3
  N12: Pins_of_Tp-4056_2.pin1, TP1.pin6

notes:
  Kevin W.
  Tp-4056
  OLED
  HM-10
  KX023
  KX023 Pins
  KX023 Sensor

custom parts:
  TP4056: A DIP stand-in part for whatever IC you want. With 6 pins on a 300mil dual inline package (DIP) footprint.
