# Fritzing sketch SmartWatchPCB (saved by Fritzing 0.9.3b)
circuit board: 3.74484cm x 5.67406cm
breadboards: 1

parts:
  U1 = ESP32S-HiLetgo [part_number=ESP32S-HiLetgo]
  OLED_screen = female pin header, 4 pins [form="♀ (female)"]
  MX30102 = female pin header, 4 pins [form="♀ (female)"]
  CJMCU231 = female pin header, 4 pins [form="♀ (female)"]

nets:
  N1: U1.3.3, OLED_screen.pin4, MX30102.pin1, CJMCU231.pin1
  N2: U1.GND, OLED_screen.pin3, MX30102.pin4, CJMCU231.pin2
  N3: U1.GPIO21, OLED_screen.pin1, MX30102.pin2, CJMCU231.pin4
  N4: U1.GPIO22, OLED_screen.pin2, MX30102.pin3, CJMCU231.pin3

notes:
  TechBoys

custom parts:
  ESP32S-HiLetgo: HiLetgo ESP-WROOM-32 ESP32 ESP-32S Development Board 2.4GHz Dual-Mode WiFi + Bluetooth Dual Cores Microcontroller The ESP32 integrated with Antenna switches, RF Balun, power amplifiers, low-noise amplifiers, filters, and management modules, and the entire solution occupies the least area of PCB. 2.4 GHz Wi-Fi plus Bluetooth dual-mode chip, with TSMC Ultra-low power consumption 40nm technology,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
